# Fritzing sketch Circuit diagram (saved by Fritzing 0.9.3b)
breadboards: 1

parts:
  Part1 = Logic Level Converter
  U1 = Sharp PC817 [package=THT]
  LED1 = smd LED [color="Red (633nm)" package="0805 [SMD]"]
  R1 = Resistor [tolerance=±5% resistance=270 package="0402 [SMD]"]
  Part2 = Arduino Uno (Rev3) - ICSP
  JP1 = Header 3 [package=screwterminal-3.5mm-3_lock.007s]
  R2 = Resistor [tolerance=±5% resistance=270 package="0402 [SMD]"]

nets:
  N1: Part1.TX2_LV, Part2.D3_PWM
  GND: Part1.GND, U1.Pin_3, Part2.GND, JP1.2
  N2: Part1.LV, Part2.5V, R2.Pin_0
  N3: Part1.HV, JP1.1
  N4: Part1.TX2_HV, LED1.anode, JP1.3
  N5: U1.Pin_1, R2.Pin_1
  N6: U1.Pin_2, Part2.D4
  N7: U1.Pin_4, R1.Pin_1
  N8: LED1.cathode, R1.Pin_0
